// Digital circuit CPU.dig as structural Verilog
module CPU (
  input  in_11,
  input  in_17,
  input  in_18,
  input  in_21,
  input  in_22,
  input  CLK_RAW,
  output [31:0] x8_s0_fp,
  output [31:0] x9_s1,
  output [31:0] x10_a0,
  output [31:0] PC,
  output [31:0] ADDR,
  output [31:0] Instr,
  output [7:0] Dout,
  output [4:0] Step,
  output [7:0] Substep,
  output [7:0] Dval,
  output [15:0] out_12,
  output [15:0] out_13,
  output [31:0] A,
  output [31:0] B,
  output [31:0] Result,
  output [31:0] out_19,
  output [11:0] CSR_Address,
  output [31:0] x11_a1,
  output [31:0] x4_tp,
  output [31:0] x5_t0,
  output [31:0] x6_t1,
  output [31:0] x7_t2,
  output [31:0] x1_ra,
  output [31:0] x2_sp,
  output [31:0] x3_gp,
  output [31:0] x12_a2,
  output [31:0] x13_a3,
  output [31:0] x14_a4,
  output [31:0] x15_a5
);

  wire ADDR_CLK, ADDR_IN, ADDR_LATCH, ALU_A, ALU_B, ALU_FLAG_LATCH, ALU_N, alu_shift_step_1_p5,
       alu_shift_step_1_p6, alu_shift_step_1_p7, and_2_out, B_INSTR, B_RUN, B_STEP, B_STOP, B_SUBSTEP,
       BUS_CLK, BUS_EN, BUT_STOP, CLK, clock_1_p7, comparator_1_eq, Const1, Const31, CSR_OUT, d_ff_1_q, ImmB,
       ImmCSR, ImmI, ImmJ, ImmS, ImmU, IRQ_OP, IRQ_OP_SnP, LASTSTEP, MEM_IN, MEM_OUT, MEPC_OUT, MTVEC_OUT,
       multiplexer_1_out, nADDR_PE, nALU_RESET, nand_1_out, nCLK, nMEM_OE, nMEM_WE, nOPDONE, not_1_out,
       nPC_CNT_PE, nREG_IN_EN, nRESET, nS_EXT, nSTEPDONE, OP_IMM_LATCH, OP_IN, OP_IN_MUX, OP_LATCH, PC_IN,
       PC_IN_LATCH, PC_OUT, PC_OUT_SnP, REG_IN, RESET, ROM_SEL, RS1, Running;
  wire [1:0] ALU_A_MUX, LEN, opcode_1_trap2, REG_IN_MUX;
  wire [2:0] ALU_B_MUX, ALU_OP;
  wire [3:0] RSA, RSB, RSD;
  wire [7:0] ROM_DATA, ROM_DIN;
  wire [15:0] ROM_ADDR;
  wire [31:12] MicroCode_d;

  Register_view register_view_1 (
    .BUS_CLK(BUS_CLK), .nREG_IN_EN(nREG_IN_EN), .REG_IN(REG_IN), .RSD(RSD), .x1_ra(x1_ra), .x2_sp(x2_sp),
    .x3_gp(x3_gp), .x4_tp(x4_tp), .x5_t0(x5_t0), .x6_t1(x6_t1), .x7_t2(x7_t2), .x8_s0_fp(x8_s0_fp),
    .x9_s1(x9_s1), .x10_a0(x10_a0), .x11_a1(x11_a1), .x12_a2(x12_a2), .x13_a3(x13_a3), .x14_a4(x14_a4),
    .x15_a5(x15_a5));
  nand nand_1 (nand_1_out, PC_OUT_SnP, OP_IN_MUX);
  Multiplexer multiplexer_1 (.sel(out_12[12]), .in_0(RS1), .in_1(ImmCSR), .out(multiplexer_1_out));
  Comparator #(.Bits(32)) comparator_1 (.a({32{1'b0}}), .b(x3_gp), .eq(comparator_1_eq));  // open: gt, lt
  LED led_1 (.in(Running));
  LED led_2 (.in(not_1_out));
  not not_1 (not_1_out, Running);
  Button #(.activeLow("true")) Stop (.out(BUT_STOP));
  Button #(.activeLow("true")) Run (.out(B_RUN));
  Button #(.activeLow("true")) One_Instruction (.out(B_INSTR));
  Button #(.activeLow("true")) One_Step (.out(B_STEP));
  Button #(.activeLow("true")) One_Substep (.out(B_SUBSTEP));
  D_FF d_ff_1 (.D(comparator_1_eq), .C(~nOPDONE), .Q(d_ff_1_q));  // open: nQ
  CSR csr_1 (
    .CLK(BUS_CLK), .INA(multiplexer_1_out), .INB(in_22), .CSR_FUNC(out_12[11:10]), .ADDR_IN(ImmI),
    .ADDR_LATCH(in_21), .nRESET(nRESET), .NEW_VAL(CSR_OUT), .ADDR(CSR_Address));
  and and_1 (B_STOP, BUT_STOP, d_ff_1_q);
  Interrupt_Controller interrupt_controller_1 (
    .BUS_CLK(BUS_CLK), .MEPC_IN(PC_OUT), .nMEPC_IN_EN(nand_1_out), .IRQ_OP_SnP(IRQ_OP_SnP),
    .MTVEC_SnP(in_18), .LASTSTEP(LASTSTEP), .IRQ(in_17), .OP_LATCH(OP_LATCH), .RESET(RESET), .nRESET(nRESET),
    .MEPC_OUT(MEPC_OUT), .IRQ_OP(IRQ_OP), .MTVEC_OUT(MTVEC_OUT), .IRQ_OP_FETCH(OP_IN_MUX), .MEPC(out_19));
  and and_2 (and_2_out, nRESET, nOPDONE);
  D_FF_AS d_ff_as_1 (.Set(~1'b1), .D(1'b1), .C(ADDR_LATCH), .Clr(~and_2_out), .Q(IRQ_OP_SnP));  // open: nQ
  DebugShift32 debugshift32_1 (.CLK(BUS_CLK), .D(ALU_A), .nEN(1'b0), .Val(A));
  DebugShift32 debugshift32_2 (.CLK(BUS_CLK), .D(ALU_B), .nEN(1'b0), .Val(B));
  DebugShift32 debugshift32_3 (.CLK(BUS_CLK), .D(ADDR_IN), .nEN(1'b0), .Val(Result));
  Reset reset_1 (.out(nRESET));
  Reset #(.invertOutput("false")) reset_2 (.out(RESET));
  Multiplexer multiplexer_2 (.sel(in_11), .in_0(ADDR_IN), .in_1(MEPC_OUT), .out(PC_IN));
  Multiplexer multiplexer_3 (.sel(OP_IN_MUX), .in_0(MEM_OUT), .in_1(IRQ_OP), .out(OP_IN));
  D_FF d_ff_2 (.D(OP_LATCH), .C(CLK), .Q(OP_IMM_LATCH));  // open: nQ
  Multiplexer #(.Selector_Bits(2)) multiplexer_4 (
    .sel(ALU_A_MUX), .in_0(RS1), .in_1(PC_OUT), .in_2(Const31), .in_3(1'b0), .out(ALU_A));
  not not_2 (nPC_CNT_PE, PC_IN_LATCH);
  Clock_driver clock_driver_1 (
    .CLK_RAW(CLK_RAW), .Stop(B_STOP), .Run(B_RUN), .One_Instruction(B_INSTR), .One_Step(B_STEP),
    .One_Substep(B_SUBSTEP), .nSTEPDONE(nSTEPDONE), .nOPDONE(nOPDONE), .nRESET(nRESET), .CLK(CLK),
    .nCLK(nCLK), .Running(Running));
  // ALU_shift_step alu_shift_step_1: pin names not known; wires that end beside it: CLK, nCLK, nALU_RESET, nSTEPDONE, alu_shift_step_1_p5, alu_shift_step_1_p6, alu_shift_step_1_p7
  PC pc_1 (
    .CLK(CLK), .BUS_CLK(BUS_CLK), .IN(PC_IN), .IN_LATCH(PC_IN_LATCH), .OUT_LATCH(LASTSTEP),
    .OUT_SnP(PC_OUT_SnP), .CNT_EN(nPC_CNT_PE), .CNT_2(OP_LATCH), .nRESET(nRESET), .OUT(PC_OUT), .PC(PC));
  OpCode opcode_1 (
    .CLK(BUS_CLK), .IN(OP_IN), .LATCH_OP(OP_LATCH), .LATCH_IMM(OP_IMM_LATCH), .SnP_IMM(BUS_EN),
    .nRESET(nRESET), .ImmI(ImmI), .ImmS(ImmS), .ImmB(ImmB), .ImmU(ImmU), .ImmJ(ImmJ), .Const1(Const1),
    .Const31(Const31), .ImmCSR(ImmCSR), .RSA(RSA), .RSB(RSB), .RSD(RSD), .OPCODE(out_12[9:5]),
    .FUNC3(out_12[12:10]), .SA_ALU(out_12[13]), .nS_EXT(nS_EXT), .SYS(out_12[15]), .TRAP2(opcode_1_trap2),
    .Instr(Instr), .DImmI(out_13));
  Multiplexer #(.Selector_Bits(3)) multiplexer_5 (
    .sel(ALU_B_MUX), .in_0(MEM_IN), .in_1(ImmI), .in_2(ImmS), .in_3(ImmB), .in_4(ImmU), .in_5(ImmJ),
    .in_6(Const1), .in_7(1'b0), .out(ALU_B));
  // Clock clock_1: pin names not known; wires that end beside it: CLK, nCLK, LEN, LASTSTEP, nRESET, out_12[4:0], clock_1_p7, nSTEPDONE, Substep, nOPDONE, clock_1_p7
  and and_3 (BUS_CLK, CLK, BUS_EN);
  // ALU alu_1: pin names not known; wires that end beside it: BUS_CLK, ALU_A, ALU_B, ALU_N, nALU_RESET, ALU_FLAG_LATCH, ALU_OP, alu_shift_step_1_p5, alu_shift_step_1_p6, alu_shift_step_1_p7, out_12[14], ADDR_IN
  or or_1 (BUS_EN, LEN[0], LEN[1]);
  Multiplexer #(.Selector_Bits(2)) multiplexer_6 (
    .sel(REG_IN_MUX), .in_0(ADDR_IN), .in_1(MEM_OUT), .in_2(MEPC_OUT), .in_3(PC_OUT), .out(REG_IN));
  // Mem mem_1: pin names not known; wires that end beside it: CLK, BUS_CLK, MEM_IN, ADDR_IN, ADDR_LATCH, ADDR_CLK, nADDR_PE, nMEM_OE, nMEM_WE, nRESET, ROM_DATA, nS_EXT, MEM_OUT, ADDR, Dout, Dval, ROM_ADDR, ROM_SEL, ROM_DIN
  // Register_bank register_bank_1: pin names not known; wires that end beside it: BUS_CLK, REG_IN, nREG_IN_EN, RSA, RSB, RSD, RESET, RS1, MEM_IN
  ROM #(.AddrBits(16), .isProgramMemory("true"), .Bits(32)) MicroCode (
    .A(out_12), .sel(1'b1),
    .D({MicroCode_d[31], REG_IN_MUX, ALU_B_MUX, ALU_A_MUX, MicroCode_d[23:22], OP_LATCH, nMEM_WE, nMEM_OE, nADDR_PE, ADDR_CLK, ADDR_LATCH, MicroCode_d[15:12], PC_OUT_SnP, PC_IN_LATCH, nREG_IN_EN, LASTSTEP, LEN, ALU_OP, ALU_FLAG_LATCH, nALU_RESET, ALU_N}));
  EEPROM #(.AddrBits(16), .Bits(8)) Firmware (.A(ROM_ADDR), .CS(ROM_SEL), .WE(~nMEM_WE), .OE(~nMEM_OE), .D(ROM_DATA));
  assign ROM_DATA = ~nMEM_WE ? ROM_DIN : 8'bz;  // DriverInvSel driverinvsel_1

  assign Step = out_12[4:0];

  // Other names for the same wires on the sheet: PC_OUT_LATCH = LASTSTEP; PC_CNT_EN = OP_LATCH; ALU_OUT = ADDR_IN;
  //   CSR_ADDR_LATCH = in_21; CSR_IN = in_22; FLAG = out_12[14]; FUNC3[2:0] = out_12[12:10]; gp[31:0] = x3_gp;
  //   IMM_SnP = BUS_EN; Mem_Dout[7:0] = Dout; Mem_Dval[7:0] = Dval; OPCODE[4:0] = out_12[9:5]; PC_IN_MUX = in_11;
  //   RS2 = MEM_IN; SA = out_12[13]; SYS = out_12[15]

  // Notes on the sheet:
  //   CLK_RAW: Hz: 5000
  //   Debug
  //   Interrupts
  //   CSR
  //   Clock
  //   ALU
  //   PC
  //   Opcode
  //   Registers
  //   Memory
  //   Microcode
  //   ROM
  //   contents of MicroCode (hex, n*v repeats v):
  //   1d1c0a8a,190202,130202,1d0242,170202,1d0242,170202,1d0242,170202,1d0242,3d0202,1d0200,
  //   41c0282,190202,130202,201d0042,201d0042,201d0042,201d0042,201d0102,0,0,0,0,0,0,0,
  //   0,0,0,0,0,1d1c0a8a,190202,130202,1d0242,170202,1d0242,170202,1d0242,170202,1d0242,
  //   3d0202,3d0202,3d0202,3d0302,0,0,0,0,0,0,0,0,0,0,0,0,0,0,0,0,0,0,1d1c0a8a,190202,130202,
  //   1d0242,170202,1d0242,170202,1d0242,170202,1d0242,3d0202,3d0202,3d0202,3d0302,0,0,
  //   0,0,0,0,0,0,0,0,0,0,0,0,0,0,0,0,1d1c0a8a,190202,130202,1d0242,170202,1d0242,170202,
  //   1d0242,170202,1d0242,3d0202,3d0202,3d0202,3d0302,0,0,0,0,0,0,0,0,0,0,0,0,0,0,0,0,
  //   0,0,1d1c0a8a,190202,130202,1d0242,170202,1d0242,170202,1d0242,170202,1d0242,3d0202,
  //   1d0200,41d0082,1d0302,0,0,0,0,0,0,0,0,0,0,0,0,0,0,0,0,0,0,1d1c0a8a,190202,130202,
  //   1d0242,170202,1d0242,170202,1d0242,170202,1d0242,3d0202,1d0200,111d0882,1d0302,0,
  //   0,0,0,0,0,0,0,0,0,0,0,0,0,0,0,0,0,1d1c0a8a,190202,130202,1d0242,170202,1d0242,170202,
  //   1d0242,170202,1d0242,3d0202,3d0202,3d0202,3d0302,0,0,0,0,0,0,0,0,0,0,0,0,0,0,0,0,
  //   0,0,1d1c0a8a,190202,130202,1d0242,170202,1d0242,170202,1d0242,170202,1d0242,3d0202,
  //   3d0202,3d0202,3d0302,0,0,0,0,0,0,0,0,0,0,0,0,0,0,0,0,0,0,1d1c0a8a,190202,130202,1d0242,
  //   170202,1d0242,170202,1d0242,170202,1d0242,3d0202,1d0200,81c0282,190202,1a0242,c0202,
  //   1c0302,0,0,0,0,0,0,0,0,0,0,0,0,0,0,0,1d1c0a8a,190202,130202,1d0242,170202,1d0242,
  //   170202,1d0242,170202,1d0242,3d0202,3d0202,3d0202,3d0302,0,0,0,0,0,0,0,0,0,0,0,0,0,
  //   0,0,0,0,0,1d1c0a8a,190202,130202,1d0242,170202,1d0242,170202,1d0242,170202,1d0242,
  //   3d0202,3d0202,3d0202,3d0302,0,0,0,0,0,0,0,0,0,0,0,0,0,0,0,0,0,0,1d1c0a8a,190202,130202,
  //   1d0242,170202,1d0242,170202,1d0242,170202,1d0242,3d0202,3d0202,3d0202,3d0302,0,0,
  //   0,0,0,0,0,0,0,0,0,0,0,0,0,0,0,0,1d1c0a8a,190202,130202,1d0242,170202,1d0242,170202,
  //   1d0242,170202,1d0242,3d0202,1d0200,1d0082,1d0302,0,0,0,0,0,0,0,0,0,0,0,0,0,0,0,0,
  //   0,0,1d1c0a8a,190202,130202,1d0242,170202,1d0242,170202,1d0242,170202,1d0242,3d0202,
  //   1d0200,131d0082,1d0302,0,0,0,0,0,0,0,0,0,0,0,0,0,0,0,0,0,0,1d1c0a8a,190202,130202,
  //   1d0242,170202,1d0242,170202,1d0242,170202,1d0242,3d0202,3d0202,3d0202,3d0302,0,0,
  //   0,0,0,0,0,0,0,0,0,0,0,0,0,0,0,0,1d1c0a8a,190202,130202,1d0242,170202,1d0242,170202,
  //   1d0242,170202,1d0242,3d0202,3d0202,3d0202,3d0302,0,0,0,0,0,0,0,0,0,0,0,0,0,0,0,0,
  //   0,0,1d1c0a8a,190202,130202,1d0242,170202,1d0242,170202,1d0242,170202,1d0242,3d0202,
  //   3d0202,3d0202,3d0302,0,0,0,0,0,0,0,0,0,0,0,0,0,0,0,0,0,0,1d1c0a8a,190202,130202,1d0242,
  //   170202,1d0242,170202,1d0242,170202,1d0242,3d0202,3d0202,3d0202,3d0302,0,0,0,0,0,0,
  //   0,0,0,0,0,0,0,0,0,0,0,0,1d1c0a8a,190202,130202,1d0242,170202,1d0242,170202,1d0242,
  //   170202,1d0242,3d0202,3d0202,3d0202,3d0302,0,0,0,0,0,0,0,0,0,0,0,0,0,0,0,0,0,0,1d1c0a8a,
  //   190202,130202,1d0242,170202,1d0242,170202,1d0242,170202,1d0242,3d0202,3d0202,3d0202,
  //   3d0302,0,0,0,0,0,0,0,0,0,0,0,0,0,0,0,0,0,0,1d1c0a8a,190202,130202,1d0242,170202,1d0242,
  //   170202,1d0242,170202,1d0242,3d0202,3d0202,3d0202,3d0302,0,0,0,0,0,0,0,0,0,0,0,0,0,
  //   0,0,0,0,0,1d1c0a8a,190202,130202,1d0242,170202,1d0242,170202,1d0242,170202,1d0242,
  //   3d0202,3d0202,3d0202,3d0302,0,0,0,0,0,0,0,0,0,0,0,0,0,0,0,0,0,0,1d1c0a8a,190202,130202,
  //   1d0242,170202,1d0242,170202,1d0242,170202,1d0242,3d0202,3d0202,3d0202,3d0302,0,0,
  //   0,0,0,0,0,0,0,0,0,0,0,0,0,0,0,0,1d1c0a8a,190202,130202,1d0242,170202,1d0242,170202,
  //   1d0242,170202,1d0242,3d0202,3d0202,3d0202,3d0302,0,0,0,0,0,0,0,0,0,0,0,0,0,0,0,0,
  //   0,0,1d1c0a8a,190202,130202,1d0242,170202,1d0242,170202,1d0242,170202,1d0242,3d0202,
  //   1d0201,1d0293,1d0206,1d0302,0,0,0,0,0,0,0,0,0,0,0,0,0,0,0,0,0,1d1c0a8a,190202,130202,
  //   1d0242,170202,1d0242,170202,1d0242,170202,1d0242,3d0202,1d0200,41d0282,1d0600,1d1d08c2,
  //   1d1d0202,191d08c2,191d08c2,191d08c2,191d0842,191d0842,191d0842,1d0302,0,0,0,0,0,0,
  //   0,0,0,1d1c0a8a,190202,130202,1d0242,170202,1d0242,170202,1d0242,170202,1d0242,3d0202,
  //   3d0202,3d0202,3d0302,0,0,0,0,0,0,0,0,0,0,0,0,0,0,0,0,0,0,1d1c0a8a,190202,130202,1d0242,
  //   170202,1d0242,170202,1d0242,170202,1d0242,3d0202,1d0200,151d0a82,1d0600,1d1d08c2,
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  //   contents of Firmware (hex, n*v repeats v):
  //   13,4,20,0,93,0,0,0,13,1,0,0,33,87,20,0,93,3,0,0,93,4,20,0,63,18,77,4c,93,0,10,0,13,
  //   1,10,0,33,87,20,0,93,3,20,0,93,4,30,0,63,1c,77,4a,93,0,30,0,13,1,70,0,33,87,20,0,
  //   93,3,a0,0,93,4,40,0,63,10,77,4a,93,0,0,0,37,81,ff,ff,33,87,20,0,b7,83,ff,ff,93,4,
  //   50,0,63,14,77,48,b7,0,0,80,13,1,0,0,33,87,20,0,b7,3,0,80,93,4,60,0,63,18,77,46,b7,
  //   0,0,80,37,81,ff,ff,33,87,20,0,b7,83,ff,7f,93,4,70,0,63,1c,77,44,93,0,0,0,37,81,0,
  //   0,13,1,f1,ff,33,87,20,0,b7,83,0,0,93,83,f3,ff,93,4,80,0,63,1c,77,42,b7,0,0,80,93,
  //   80,f0,ff,13,1,0,0,33,87,20,0,b7,3,0,80,93,83,f3,ff,93,4,90,0,63,1c,77,40,b7,0,0,80,
  //   93,80,f0,ff,37,81,0,0,13,1,f1,ff,33,87,20,0,b7,83,0,80,93,83,e3,ff,93,4,a0,0,63,1a,
  //   77,3e,b7,0,0,80,37,81,0,0,13,1,f1,ff,33,87,20,0,b7,83,0,80,93,83,f3,ff,93,4,b0,0,
  //   63,1a,77,3c,b7,0,0,80,93,80,f0,ff,37,81,ff,ff,33,87,20,0,b7,83,ff,7f,93,83,f3,ff,
  //   93,4,c0,0,63,1a,77,3a,93,0,0,0,13,1,f0,ff,33,87,20,0,93,3,f0,ff,93,4,d0,0,63,1e,77,
  //   38,93,0,f0,ff,13,1,10,0,33,87,20,0,93,3,0,0,93,4,e0,0,63,12,77,38,93,0,f0,ff,13,1,
  //   f0,ff,33,87,20,0,93,3,e0,ff,93,4,f0,0,63,16,77,36,93,0,10,0,37,1,0,80,13,1,f1,ff,
  //   33,87,20,0,b7,3,0,80,93,4,0,1,63,18,77,34,93,0,d0,0,13,1,b0,0,b3,80,20,0,93,3,80,
  //   1,93,4,10,1,63,9c,70,32,93,0,e0,0,13,1,b0,0,33,81,20,0,93,3,90,1,93,4,20,1,63,10,
  //   71,32,93,0,d0,0,b3,80,10,0,93,3,a0,1,93,4,30,1,63,96,70,30,13,2,0,0,93,0,d0,0,13,
  //   1,b0,0,33,87,20,0,13,3,7,0,13,2,12,0,93,2,20,0,e3,14,52,fe,93,3,80,1,93,4,40,1,63,
  //   10,73,2e,13,2,0,0,93,0,e0,0,13,1,b0,0,33,87,20,0,13,0,0,0,13,3,7,0,13,2,12,0,93,2,
  //   20,0,e3,12,52,fe,93,3,90,1,93,4,50,1,63,18,73,2a,13,2,0,0,93,0,f0,0,13,1,b0,0,33,
  //   87,20,0,13,0,0,0,13,0,0,0,13,3,7,0,13,2,12,0,93,2,20,0,e3,10,52,fe,93,3,a0,1,93,4,
  //   60,1,63,1e,73,26,13,2,0,0,93,0,d0,0,13,1,b0,0,33,87,20,0,13,2,12,0,93,2,20,0,e3,16,
  //   52,fe,93,3,80,1,93,4,70,1,63,1a,77,24,13,2,0,0,93,0,e0,0,13,1,b0,0,13,0,0,0,33,87,
  //   20,0,13,2,12,0,93,2,20,0,e3,14,52,fe,93,3,90,1,93,4,80,1,63,14,77,22,13,2,0,0,93,
  //   0,f0,0,13,1,b0,0,13,0,0,0,13,0,0,0,33,87,20,0,13,2,12,0,93,2,20,0,e3,12,52,fe,93,
  //   3,a0,1,93,4,90,1,63,1c,77,1e,13,2,0,0,93,0,d0,0,13,0,0,0,13,1,b0,0,33,87,20,0,13,
  //   2,12,0,93,2,20,0,e3,14,52,fe,93,3,80,1,93,4,a0,1,63,16,77,1c,13,2,0,0,93,0,e0,0,13,
  //   0,0,0,13,1,b0,0,13,0,0,0,33,87,20,0,13,2,12,0,93,2,20,0,e3,12,52,fe,93,3,90,1,93,
  //   4,b0,1,63,1e,77,18,13,2,0,0,93,0,f0,0,13,0,0,0,13,0,0,0,13,1,b0,0,33,87,20,0,13,2,
  //   12,0,93,2,20,0,e3,12,52,fe,93,3,a0,1,93,4,c0,1,63,16,77,16,13,2,0,0,13,1,b0,0,93,
  //   0,d0,0,33,87,20,0,13,2,12,0,93,2,20,0,e3,16,52,fe,93,3,80,1,93,4,d0,1,63,12,77,14,
  //   13,2,0,0,13,1,b0,0,93,0,e0,0,13,0,0,0,33,87,20,0,13,2,12,0,93,2,20,0,e3,14,52,fe,
  //   93,3,90,1,93,4,e0,1,63,1c,77,10,13,2,0,0,13,1,b0,0,93,0,f0,0,13,0,0,0,13,0,0,0,33,
  //   87,20,0,13,2,12,0,93,2,20,0,e3,12,52,fe,93,3,a0,1,93,4,f0,1,63,14,77,e,13,2,0,0,13,
  //   1,b0,0,13,0,0,0,93,0,d0,0,33,87,20,0,13,2,12,0,93,2,20,0,e3,14,52,fe,93,3,80,1,93,
  //   4,0,2,63,1e,77,a,13,2,0,0,13,1,b0,0,13,0,0,0,93,0,e0,0,13,0,0,0,33,87,20,0,13,2,12,
  //   0,93,2,20,0,e3,12,52,fe,93,3,90,1,93,4,10,2,63,16,77,8,13,2,0,0,13,1,b0,0,13,0,0,
  //   0,13,0,0,0,93,0,f0,0,33,87,20,0,13,2,12,0,93,2,20,0,e3,12,52,fe,93,3,a0,1,93,4,20,
  //   2,63,1e,77,4,93,0,f0,0,33,1,10,0,93,3,f0,0,93,4,30,2,63,14,71,4,93,0,0,2,33,81,0,
  //   0,93,3,0,2,93,4,40,2,63,1a,71,2,b3,0,0,0,93,3,0,0,93,4,50,2,63,92,70,2,93,0,0,1,13,
  //   1,e0,1,33,80,20,0,93,3,0,0,93,4,60,2,63,16,70,0,63,4,90,0,6f,0,40,1,63,80,4,0,93,
  //   10,4,1,b3,81,90,0,6f,0,0,0,13,4,30,0,93,0,0,0,13,1,0,0,33,87,20,40,93,3,0,0,93,4,
  //   20,0,63,18,77,4a,93,0,10,0,13,1,10,0,33,87,20,40,93,3,0,0,93,4,30,0,63,1c,77,48,93,
  //   0,30,0,13,1,70,0,33,87,20,40,93,3,c0,ff,93,4,40,0,63,10,77,48,93,0,0,0,37,81,ff,ff,
  //   33,87,20,40,b7,83,0,0,93,4,50,0,63,14,77,46,b7,0,0,80,13,1,0,0,33,87,20,40,b7,3,0,
  //   80,93,4,60,0,63,18,77,44,b7,0,0,80,37,81,ff,ff,33,87,20,40,b7,83,0,80,93,4,70,0,63,
  //   1c,77,42,93,0,0,0,37,81,0,0,13,1,f1,ff,33,87,20,40,b7,83,ff,ff,93,83,13,0,93,4,80,
  //   0,63,1c,77,40,b7,0,0,80,93,80,f0,ff,13,1,0,0,33,87,20,40,b7,3,0,80,93,83,f3,ff,93,
  //   4,90,0,63,1c,77,3e,b7,0,0,80,93,80,f0,ff,37,81,0,0,13,1,f1,ff,33,87,20,40,b7,83,ff,
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endmodule
